# Fritzing sketch TempHumLcd_board_dht11_OHNE_widerstand (saved by Fritzing 0.9.3b)
breadboards: 1

parts:
  DHT11-Sensor = DHT11 Humitidy and Temperature Sensor
  Arduino_Nano = Arduino Nano (Rev3.0)
  LCD_(I2C-Schnittstelle) = LCD1602-I2C

nets:
  VDD: DHT11-Sensor.VDD, Arduino_Nano.5V, LCD_(I2C-Schnittstelle).VCC
  N1: DHT11-Sensor.DATA, Arduino_Nano.D2
  GND: DHT11-Sensor.GND, Arduino_Nano.GND, LCD_(I2C-Schnittstelle).GND
  N2: Arduino_Nano.A5, LCD_(I2C-Schnittstelle).SCL
  N3: Arduino_Nano.A4, LCD_(I2C-Schnittstelle).SDA

custom parts:
  DHT11 Humitidy and Temperature Sensor: DHT11 Humidity and Temperature Sensor
  LCD1602-I2C: A standard character display, usually with 2x16 characters. Comes in many colors with LCM1602 IIC attached.
