# Fritzing sketch TempHumLcd_dht11_OHNE_widerstand - Kopie (saved by Fritzing 0.9.3b)
breadboards: 1

parts:
  DHT1 = DHT11 Humitidy and Temperature Sensor
  Bauteil1 = Arduino Nano (Rev3.0)
  Bauteil2 = LCD1602-I2C

nets:
  N1: DHT1.VDD, Bauteil1.D2
  N2: DHT1.DATA, Bauteil1.3V3
  GND: DHT1.GND, Bauteil1.GND, Bauteil2.GND
  5V: Bauteil1.5V, Bauteil2.VCC
  N3: Bauteil1.A5, Bauteil2.SCL
  N4: Bauteil1.A4, Bauteil2.SDA

custom parts:
  DHT11 Humitidy and Temperature Sensor: DHT11 Humidity and Temperature Sensor
  LCD1602-I2C: A standard character display, usually with 2x16 characters. Comes in many colors with LCM1602 IIC attached.
