# Fritzing sketch dht11_OHNE_widerstand (saved by Fritzing 0.9.3b)
breadboards: 1

parts:
  DHT1 = DHT11 Humitidy and Temperature Sensor
  Bauteil1 = Arduino Nano (Rev3.0)

nets:
  N1: DHT1.VDD, Bauteil1.D2
  N2: DHT1.DATA, Bauteil1.5V
  GND: DHT1.GND, Bauteil1.GND

custom parts:
  DHT11 Humitidy and Temperature Sensor: DHT11 Humidity and Temperature Sensor
