# Fritzing sketch arduino_nano_sensor_ultrasound (saved by Fritzing 0.9.3b)

parts:
  Bauteil1 = Arduino Nano (Rev3.0)
  hc-sr1 = hc-sr04

nets:
  N1: Bauteil1.D8, hc-sr1.Trig
  N2: Bauteil1.D9, hc-sr1.Echo
  GND: Bauteil1.GND, hc-sr1.GND
  5V: Bauteil1.5V, hc-sr1.VCC
