# Fritzing sketch led_blink (saved by Fritzing 0.9.3b)
breadboards: 1

parts:
  Bauteil1 = Arduino Nano (Rev3.0)
  R1 = Resistor [tolerance=±5% resistance=1k package=THT]
  LED1 = LED - 5mm [color="Red (633nm)" package="5 mm [THT]"]

nets:
  N1: Bauteil1.D6, R1.Pin_1
  N2: Bauteil1.GND, LED1.anode
  N3: R1.Pin_0, LED1.cathode
